// Logisim project cdm16.circ as structural Verilog: 20 circuits, main circuit cdm16
module cdm16 (
  input  [15:0] data_in,
  input  EXC,
  input  [5:0] exc_vec,
  input  IRQ,
  input  [5:0] int_vec,
  input  clock,
  input  hold,
  output [15:0] SP,
  output [15:0] PC,
  output [15:0] PS,
  output [15:0] address,
  output mem,
  output data_ins_prime,
  output [15:0] R0,
  output rd_wr_prime,
  output [15:0] R1,
  output [15:0] R2,
  output word,
  output [15:0] R3,
  output [15:0] R4,
  output [15:0] R5,
  output [15:0] data_out,
  output [15:0] R6,
  output [15:0] FP,
  output [1:0] status,
  output IAck,
  output fetch
);

  wire _0op, _1op, _2op, alu2, alu3, alu3_ind, alu_asrtD, and_1_out, and_2_out, and_4_out, and_6_out,
       and_7_out, and_9_out, and_10_out, and_11_out, and_12_out, and_13_out, and_14_out, and_15_out,
       and_16_out, and_17_out, and_18_out, and_19_out, and_20_out, and_21_out, and_22_out, and_23_out,
       and_24_out, and_28_out, and_29_out, and_30_out, and_33_out, and_35_out, and_37_out, and_39_out,
       and_40_out, and_41_out, and_46_out, and_47_out, and_48_out, arith_carry, br_abs, br_abs_d, br_abs_nop,
       br_rel_n, br_rel_nop, br_rel_p, branch_logic_1_go, clk, clk_inhibit, clk_no_inhibit, comparator_1_eq,
       comparator_3_eq, cout, critical_fault, CUT, d_ff_1_q, d_ff_2_qn, decoder_1_out0, decoder_1_out1,
       decoder_1_out2, decoder_1_out3, decoder_1_out4, decoder_1_out5, decoder_1_out6, decoder_1_out7,
       decoder_2_out0, decoder_2_out1, decoder_2_out2, decoder_2_out3, decoder_2_out4, decoder_2_out5,
       decoder_2_out6, decoder_2_out7, decoder_3_out0, decoder_3_out1, decoder_3_out2, decoder_3_out3,
       decoder_3_out4, decoder_3_out5, decoder_3_out6, decoder_3_out7, decoder_4_out0, decoder_4_out2,
       decoder_4_out5, decoder_4_out6, decoder_4_out7, demultiplexer_1_out0, di, double_fault, ei, exc_latch,
       exc_trig_invalid_inst, exc_trig_pc, exc_trig_sp, exc_triggered, fp_asrt0, halt, imm6, imm9, imm_asrt1,
       imm_asrtD, imm_extend_negative, imm_shift, inc_address, \int , io_phase, jsr, latch_int, mem2, mem3,
       multiplexer_8_out, nor_1_out, not_1_out, not_2_out, not_3_out, not_4_out, not_5_out, not_6_out,
       not_7_out, not_8_out, not_9_out, not_10_out, not_11_out, not_12_out, not_13_out, not_14_out, or_1_out,
       or_2_out, or_3_out, or_4_out, or_5_out, or_6_out, or_10_out, or_12_out, or_13_out, or_14_out,
       or_16_out, or_18_out, or_19_out, or_20_out, or_22_out, or_23_out, pc_asrt0, pc_asrtD, pc_inc,
       pc_latch, priority_encoder_2_gs, priority_encoder_4_gs, ps_asrtD, ps_latch_flags, ps_latch_word,
       r_asrt0, r_asrt1, r_asrtD, r_latch, reset_exc, rti, s_r_ff_1_q, s_r_ff_2_q, s_r_ff_3_q, shifts,
       sign_extend, sp_asrt0, sp_asrtD, sp_dec, sp_inc, sp_latch, startup, \wait , word_t;
  wire [0:0] or_15_out;
  wire [2:0] alu_func, alu_op_d0, alu_op_d1, alu_op_type, CVZN, exc_internal_vec, multiplexer_1_out,
       multiplexer_19_out, multiplexer_20_out, phase, priority_encoder_2_out, priority_encoder_3_out,
       priority_encoder_4_out, rs0, rs1;
  wire [2:1] imm6_d;
  wire [3:0] bit_extender_9_out, br_abs_flags_d, multiplexer_7_out, multiplexer_10_out, ps_flags;
  wire [3:3] br_rel_flags_d;
  wire [5:0] exc_vec_t;
  wire [15:0] bit_extender_1_out, bit_extender_2_out, bit_extender_3_out, bit_extender_4_out,
       bit_extender_5_out, bit_extender_6_out, bit_extender_7_out, bit_extender_8_out, bus_control_1_to_bus,
       imm, multiplexer_2_out, multiplexer_3_out, multiplexer_4_out, multiplexer_5_out, multiplexer_6_out,
       multiplexer_9_out, multiplexer_12_out, multiplexer_13_out, or_8_out, or_17_out, pc_register_1_mon,
       pull_resistor_1_node, pull_resistor_2_node, pull_resistor_3_node, shifter_1_out, shifter_2_out,
       sp_register_1_mon;
  wire [15:13] register_11_q;
  wire [27:0] multiplexer_17_out, rom_1_data, rom_2_data;

  not not_1 (not_1_out, CUT);
  Register #(.width(6), .trigger("falling")) register_1 (
    .D(exc_vec), .en(EXC), .Q(exc_vec_t), .clk(clk_no_inhibit));  // open: clr
  D_Flip_Flop #(.trigger("low")) d_ff_1 (.clk(clock), .D(hold), .Q(d_ff_1_q));  // open: Qn, preset, en, reset
  S_R_Flip_Flop #(.trigger("falling")) s_r_ff_1 (
    .S(\wait ), .clk(clock), .R(IRQ), .Q(s_r_ff_1_q));  // open: Qn, preset, reset, en
  or or_1 (or_1_out, s_r_ff_2_q, s_r_ff_3_q);
  S_R_Flip_Flop #(.trigger("falling")) s_r_ff_2 (
    .S(halt), .clk(clk_no_inhibit), .R(1'b0), .Q(s_r_ff_2_q));  // open: Qn, preset, reset, en
  S_R_Flip_Flop #(.trigger("falling")) s_r_ff_3 (
    .S(critical_fault), .clk(clk_no_inhibit), .R(1'b0), .Q(s_r_ff_3_q));  // open: Qn, preset, reset, en
  Counter #(.width(3), .max('h7), .trigger("falling")) counter_1 (
    .load(CUT), .D(3'b000), .count(not_1_out), .Q(phase), .clk(clk));  // open: carry, clr
  Decoder #(.select(3), .enable("false")) decoder_1 (
    .out0(decoder_1_out0), .out1(decoder_1_out1), .out2(decoder_1_out2), .out3(decoder_1_out3),
    .out4(decoder_1_out4), .out5(decoder_1_out5), .out6(decoder_1_out6), .out7(decoder_1_out7),
    .sel(br_abs_flags_d[2:0]));
  or or_2 (or_2_out, d_ff_1_q, s_r_ff_1_q, or_1_out);
  not not_2 (not_2_out, or_2_out);
  nor nor_1 (nor_1_out, phase[0], phase[1], phase[2]);
  D_Flip_Flop #(.trigger("falling")) d_ff_2 (
    .clk(clk), .D(d_ff_2_qn), .Qn(d_ff_2_qn), .en(CUT));  // open: Q, preset, reset
  Pull_Resistor pull_resistor_1 (.node(pull_resistor_1_node));
  Pull_Resistor pull_resistor_2 (.node(pull_resistor_2_node));
  Pull_Resistor pull_resistor_3 (.node(pull_resistor_3_node));
  and and_1 (and_1_out, decoder_1_out0, r_latch);
  and and_2 (and_2_out, r_asrtD, decoder_1_out0);
  not not_3 (not_3_out, clk_inhibit);
  and and_3 (clk_no_inhibit, clock, not_2_out);
  Priority_Encoder #(.select(2)) priority_encoder_1 (
    .in0(1'b1), .in1(s_r_ff_1_q), .in2(s_r_ff_2_q), .in3(s_r_ff_3_q), .out(status));  // open: gs, en_out, en_in
  and and_4 (and_4_out, startup, clk);
  and and_5 (fetch, nor_1_out, d_ff_2_qn);
  assign pull_resistor_1_node = decoder_2_out0 ? R0 : 16'bz;  // Controlled_Buffer controlled_buffer_1
  assign pull_resistor_1_node = decoder_2_out1 ? R1 : 16'bz;  // Controlled_Buffer controlled_buffer_2
  assign pull_resistor_2_node = decoder_3_out0 ? R0 : 16'bz;  // Controlled_Buffer controlled_buffer_3
  Register #(.width(16), .trigger("falling")) register_2 (
    .D(pull_resistor_3_node), .en(and_1_out), .Q(R0), .clk(clk));  // open: clr
  Register #(.width(16), .trigger("falling")) register_3 (
    .D(pull_resistor_3_node), .en(and_6_out), .Q(R1), .clk(clk));  // open: clr
  and and_6 (and_6_out, decoder_1_out1, r_latch);
  and and_7 (and_7_out, r_asrtD, decoder_1_out1);
  assign pull_resistor_3_node = and_2_out ? R0 : 16'bz;  // Controlled_Buffer controlled_buffer_4
  or or_3 (or_3_out, or_4_out, EXC);
  or or_4 (or_4_out, exc_trig_invalid_inst, exc_trig_pc, exc_trig_sp);
  and and_8 (clk, not_3_out, clk_no_inhibit);
  D_Flip_Flop #(.trigger("falling")) d_ff_3 (.clk(and_4_out), .D(CUT), .Qn(startup));  // open: Q, preset, en, reset
  assign pull_resistor_1_node = decoder_2_out2 ? R2 : 16'bz;  // Controlled_Buffer controlled_buffer_5
  assign pull_resistor_2_node = decoder_3_out2 ? R2 : 16'bz;  // Controlled_Buffer controlled_buffer_6
  assign pull_resistor_2_node = decoder_3_out1 ? R1 : 16'bz;  // Controlled_Buffer controlled_buffer_7
  Register #(.width(16), .trigger("falling")) register_4 (
    .D(pull_resistor_3_node), .en(and_9_out), .Q(R2), .clk(clk));  // open: clr
  and and_9 (and_9_out, decoder_1_out2, r_latch);
  and and_10 (and_10_out, r_asrtD, decoder_1_out2);
  assign pull_resistor_3_node = and_7_out ? R1 : 16'bz;  // Controlled_Buffer controlled_buffer_8
  assign pull_resistor_3_node = and_10_out ? R2 : 16'bz;  // Controlled_Buffer controlled_buffer_9
  and and_11 (and_11_out, or_4_out, EXC);
  Priority_Encoder priority_encoder_2 (
    .in1(exc_trig_sp), .in2(exc_trig_pc), .in3(exc_trig_invalid_inst), .in7(EXC),
    .out(priority_encoder_2_out), .gs(priority_encoder_2_gs));  // open: in0, in4, in5, in6, en_in, en_out
  assign pull_resistor_1_node = decoder_2_out3 ? R3 : 16'bz;  // Controlled_Buffer controlled_buffer_10
  assign pull_resistor_2_node = decoder_3_out3 ? R3 : 16'bz;  // Controlled_Buffer controlled_buffer_11
  Register #(.width(16), .trigger("falling")) register_5 (
    .D(pull_resistor_3_node), .en(and_12_out), .Q(R3), .clk(clk));  // open: clr
  and and_12 (and_12_out, decoder_1_out3, r_latch);
  and and_13 (and_13_out, decoder_1_out4, r_latch);
  and and_14 (and_14_out, r_asrtD, decoder_1_out4);
  and and_15 (and_15_out, r_asrtD, decoder_1_out3);
  assign pull_resistor_3_node = and_15_out ? R3 : 16'bz;  // Controlled_Buffer controlled_buffer_12
  and and_16 (and_16_out, or_3_out, exc_latch);
  or or_5 (or_5_out, rti, \int );
  or or_6 (or_6_out, and_11_out, and_16_out, or_5_out);
  Multiplexer #(.width(3), .enable("false")) multiplexer_1 (
    .in0(priority_encoder_2_out), .in1(3'b100), .out(multiplexer_1_out), .sel(or_6_out));
  Comparator #(.width(3), .mode("unsigned")) comparator_1 (
    .a(exc_internal_vec), .b(3'b111), .eq(comparator_1_eq));  // open: gt, lt
  assign bit_extender_1_out = {{13{1'b0}}, exc_internal_vec};  // Bit_Extender bit_extender_1
  assign bit_extender_2_out = {{10{1'b0}}, exc_vec_t};  // Bit_Extender bit_extender_2
  assign bit_extender_3_out = {{10{1'b0}}, exc_vec};  // Bit_Extender bit_extender_3
  and and_17 (and_17_out, EXC, fetch);
  assign pull_resistor_1_node = decoder_2_out4 ? R4 : 16'bz;  // Controlled_Buffer controlled_buffer_13
  assign pull_resistor_1_node = decoder_2_out5 ? R5 : 16'bz;  // Controlled_Buffer controlled_buffer_14
  assign pull_resistor_2_node = decoder_3_out4 ? R4 : 16'bz;  // Controlled_Buffer controlled_buffer_15
  Register #(.width(16), .trigger("falling")) register_6 (
    .D(pull_resistor_3_node), .en(and_13_out), .Q(R4), .clk(clk));  // open: clr
  Register #(.width(16), .trigger("falling")) register_7 (
    .D(pull_resistor_3_node), .en(and_18_out), .Q(R5), .clk(clk));  // open: clr
  and and_18 (and_18_out, decoder_1_out5, r_latch);
  and and_19 (and_19_out, r_asrtD, decoder_1_out5);
  assign pull_resistor_3_node = and_14_out ? R4 : 16'bz;  // Controlled_Buffer controlled_buffer_16
  Register #(.width(3), .trigger("falling")) register_8 (
    .D(multiplexer_1_out), .en(priority_encoder_2_gs), .Q(exc_internal_vec), .clk(clk_no_inhibit));  // open: clr
  Multiplexer #(.width(16), .enable("false")) multiplexer_2 (
    .in0(bit_extender_1_out), .in1(bit_extender_2_out), .out(multiplexer_2_out), .sel(comparator_1_eq));
  assign pull_resistor_1_node = decoder_2_out6 ? R6 : 16'bz;  // Controlled_Buffer controlled_buffer_17
  assign pull_resistor_2_node = decoder_3_out5 ? R5 : 16'bz;  // Controlled_Buffer controlled_buffer_18
  assign pull_resistor_2_node = decoder_3_out6 ? R6 : 16'bz;  // Controlled_Buffer controlled_buffer_19
  Register #(.width(16), .trigger("falling")) register_9 (
    .D(pull_resistor_3_node), .en(and_20_out), .Q(R6), .clk(clk));  // open: clr
  and and_20 (and_20_out, decoder_1_out6, r_latch);
  and and_21 (and_21_out, r_asrtD, decoder_1_out6);
  assign pull_resistor_3_node = and_21_out ? R6 : 16'bz;  // Controlled_Buffer controlled_buffer_20
  assign pull_resistor_3_node = and_19_out ? R5 : 16'bz;  // Controlled_Buffer controlled_buffer_21
  S_R_Flip_Flop #(.trigger("falling")) s_r_ff_4 (
    .S(priority_encoder_2_gs), .clk(clk_no_inhibit), .R(reset_exc), .Q(exc_latch));  // open: Qn, preset, reset, en
  assign bit_extender_4_out = {{10{1'b0}}, int_vec};  // Bit_Extender bit_extender_4
  Multiplexer #(.width(16), .enable("false")) multiplexer_3 (
    .in0(bit_extender_4_out), .in1(multiplexer_4_out), .out(multiplexer_3_out), .sel(exc_triggered));
  Multiplexer #(.width(16), .enable("false")) multiplexer_4 (
    .in0(multiplexer_2_out), .in1(bit_extender_3_out), .out(multiplexer_4_out), .sel(and_17_out));
  and and_22 (and_22_out, IRQ, PS[15]);
  assign pull_resistor_1_node = decoder_2_out7 ? FP : 16'bz;  // Controlled_Buffer controlled_buffer_22
  assign pull_resistor_2_node = decoder_3_out7 ? FP : 16'bz;  // Controlled_Buffer controlled_buffer_23
  Register #(.width(16), .trigger("falling")) register_10 (
    .D(pull_resistor_3_node), .en(and_23_out), .Q(FP), .clk(clk));  // open: clr
  and and_23 (and_23_out, decoder_1_out7, r_latch);
  and and_24 (and_24_out, r_asrtD, decoder_1_out7);
  assign pull_resistor_3_node = and_24_out ? FP : 16'bz;  // Controlled_Buffer controlled_buffer_24
  and and_25 (critical_fault, double_fault, priority_encoder_2_gs);
  or or_7 (exc_triggered, priority_encoder_2_gs, exc_latch);
  assign or_8_out = multiplexer_3_out | 16'h8000;  // OR_Gate or_8, 16 bits wide
  and and_26 (IAck, fetch, and_22_out);
  or or_9 (latch_int, and_22_out, exc_triggered);
  and and_27 (reset_exc, exc_triggered, fetch);
  assign pull_resistor_1_node = fp_asrt0 ? FP : 16'bz;  // Controlled_Buffer controlled_buffer_25
  Multiplexer #(.width(16), .enable("false")) multiplexer_5 (
    .in0(pull_resistor_3_node), .in1(or_8_out), .out(multiplexer_5_out), .sel(latch_int));
  Multiplexer #(.width(16), .enable("false")) multiplexer_6 (
    .in0(multiplexer_5_out), .in1(16'h8200), .out(multiplexer_6_out), .sel(startup));
  not not_4 (not_4_out, fetch);
  Decoder #(.select(3), .disabled(0)) decoder_2 (
    .out0(decoder_2_out0), .out1(decoder_2_out1), .out2(decoder_2_out2), .out3(decoder_2_out3),
    .out4(decoder_2_out4), .out5(decoder_2_out5), .out6(decoder_2_out6), .out7(decoder_2_out7), .sel(rs0),
    .en(r_asrt0));
  Decoder #(.select(3), .disabled(0)) decoder_3 (
    .out0(decoder_3_out0), .out1(decoder_3_out1), .out2(decoder_3_out2), .out3(decoder_3_out3),
    .out4(decoder_3_out4), .out5(decoder_3_out5), .out6(decoder_3_out6), .out7(decoder_3_out7), .sel(rs1),
    .en(r_asrt1));
  Register #(.width(16), .trigger("falling")) register_11 (
    .D(multiplexer_6_out), .en(fetch),
    .Q({register_11_q, br_rel_flags_d[3], alu_op_d1, alu_op_d0, imm6_d, br_abs_flags_d}), .clk(clk),
    .clr(and_28_out));
  and and_28 (and_28_out, fetch, not_4_out);
  Decoder #(.select(3), .disabled(0), .enable("false")) decoder_4 (
    .out0(decoder_4_out0), .out1(_1op), .out2(decoder_4_out2), .out3(imm6), .out4(imm9),
    .out5(decoder_4_out5), .out6(decoder_4_out6), .out7(decoder_4_out7), .sel(register_11_q));
  Comparator #(.width(16), .mode("unsigned")) comparator_2 (
    .a(16'h8004), .b({register_11_q, br_rel_flags_d[3], alu_op_d1, alu_op_d0, imm6_d, br_abs_flags_d}),
    .eq(double_fault));  // open: gt, lt
  assign pull_resistor_1_node = sp_asrt0 ? SP : 16'bz;  // Controlled_Buffer controlled_buffer_26
  // Probe on sp_register_1_mon
  sp_register sp_register_1 (
    .In(pull_resistor_3_node), .plus_2(sp_inc), .en(sp_latch), .minus_2(sp_dec), .clk(clk),
    .Mon(sp_register_1_mon), .Out(SP));  // open: clr
  assign pull_resistor_2_node = imm_asrt1 ? imm : 16'bz;  // Controlled_Buffer controlled_buffer_27
  assign pull_resistor_3_node = imm_asrtD ? imm : 16'bz;  // Controlled_Buffer controlled_buffer_28
  Demultiplexer #(.disabled(0), .enable("false")) demultiplexer_1 (
    .out0(demultiplexer_1_out0), .out1(shifts), .in(decoder_4_out0), .sel(br_rel_flags_d[3]));
  Demultiplexer #(.select(2), .disabled(0), .enable("false")) demultiplexer_2 (
    .out0(_2op), .out1(alu3_ind), .out2(mem2), .out3(alu2), .in(decoder_4_out2),
    .sel({br_rel_flags_d[3], alu_op_d1[2]}));
  Demultiplexer #(.disabled(0), .enable("false")) demultiplexer_3 (
    .out0(mem3), .out1(alu3), .in(decoder_4_out5), .sel(br_rel_flags_d[3]));
  assign pull_resistor_3_node = sp_asrtD ? SP : 16'bz;  // Controlled_Buffer controlled_buffer_29
  Demultiplexer #(.disabled(0), .enable("false")) demultiplexer_4 (
    .out0(_0op), .out1(br_abs_d), .in(demultiplexer_1_out0), .sel(alu_op_d1[2]));
  Multiplexer #(.width(4), .enable("false")) multiplexer_7 (
    .in0({br_rel_flags_d[3], alu_op_d1}), .in1(br_abs_flags_d), .out(multiplexer_7_out), .sel(br_abs_d));
  branch_logic branch_logic_1 (.cccc(multiplexer_7_out), .CVZN(ps_flags), .go(branch_logic_1_go));
  assign pull_resistor_1_node = pc_asrt0 ? PC : 16'bz;  // Controlled_Buffer controlled_buffer_30
  // Probe on pc_register_1_mon
  and and_29 (and_29_out, pc_inc, not_8_out);
  pc_register pc_register_1 (
    .In(pull_resistor_3_node), .en(pc_latch), .plus_2(and_29_out), .Out(PC), .clk(clk),
    .Mon(pc_register_1_mon), .asrt_inc(and_30_out), .inverse_inc(exc_triggered));  // open: clr
  and and_30 (and_30_out, jsr, pc_asrtD);
  and and_31 (br_abs_nop, br_abs_d, not_5_out);
  not not_5 (not_5_out, br_abs);
  and and_32 (br_abs, br_abs_d, branch_logic_1_go);
  and and_33 (and_33_out, decoder_4_out6, not_6_out);
  not not_6 (not_6_out, br_rel_n);
  and and_34 (br_rel_n, decoder_4_out6, branch_logic_1_go);
  and and_35 (and_35_out, decoder_4_out7, not_7_out);
  not not_7 (not_7_out, br_rel_p);
  and and_36 (br_rel_p, decoder_4_out7, branch_logic_1_go);
  not not_8 (not_8_out, br_rel_nop);
  assign pull_resistor_3_node = pc_asrtD ? PC : 16'bz;  // Controlled_Buffer controlled_buffer_31
  Multiplexer #(.enable("false")) multiplexer_8 (
    .in0(and_37_out), .in1(PS[3]), .out(multiplexer_8_out), .sel(arith_carry));
  alu alu_1 (
    .A(pull_resistor_1_node), .B(pull_resistor_2_node), .Cin(multiplexer_8_out), .func(alu_func),
    .op_type(alu_op_type), .C(cout), .V(CVZN[2]), .Z(CVZN[1]), .N(CVZN[0]), .S(address),
    .shift_count(alu_op_d0));
  or or_10 (or_10_out, alu_op_d1[1], alu_op_d1[2], br_rel_flags_d[3]);
  not not_9 (not_9_out, br_abs_flags_d[3]);
  or or_11 (br_rel_nop, and_33_out, and_35_out);
  and and_37 (and_37_out, mem, inc_address);
  assign pull_resistor_3_node = alu_asrtD ? address : 16'bz;  // Controlled_Buffer controlled_buffer_32
  and and_38 (\int , imm9, not_10_out);
  not not_10 (not_10_out, or_10_out);
  Decoder #(.select(2), .disabled(0)) decoder_5 (
    .out0(halt), .out1(\wait ), .out2(ei), .out3(di), .sel(br_abs_flags_d[1:0]), .en(and_39_out));
  and and_39 (and_39_out, and_40_out, not_11_out);
  not not_11 (not_11_out, exc_triggered);
  and and_40 (and_40_out, br_abs_flags_d[2], not_9_out, _0op);
  or or_12 (or_12_out, shifts, alu2);
  assign bit_extender_5_out = {{7{1'b0}}, {alu_op_d0, imm6_d, br_abs_flags_d}};  // Bit_Extender bit_extender_5
  assign bit_extender_6_out = {{7{1'b1}}, {alu_op_d0, imm6_d, br_abs_flags_d}};  // Bit_Extender bit_extender_6
  Multiplexer #(.select(2), .width(16), .disabled(0), .enable("false")) multiplexer_9 (
    .in0(bit_extender_5_out), .in1(bit_extender_6_out), .in2(bit_extender_7_out), .in3(bit_extender_8_out),
    .out(multiplexer_9_out), .sel({imm6, imm_extend_negative}));
  assign bit_extender_7_out = {{10{1'b0}}, {alu_op_d0, imm6_d, br_abs_flags_d[3]}};  // Bit_Extender bit_extender_7
  assign bit_extender_8_out = {{10{1'b1}}, {alu_op_d0, imm6_d, br_abs_flags_d[3]}};  // Bit_Extender bit_extender_8
  LED led_1 (.in(PS[15]));
  LED led_2 (.in(clk));
  // Probe on ps_flags
  ps_register ps_register_1 (
    .flags({cout, CVZN}), .word(pull_resistor_3_node), .clk(clk), .out(PS), .out_flags(ps_flags),
    .latch_flags(ps_latch_flags), .latch_word(ps_latch_word), .ei(ei), .di(di));
  or or_13 (or_13_out, br_abs_nop, br_rel_nop);
  LED led_3 (.in(clk_no_inhibit));
  assign pull_resistor_3_node = ps_asrtD ? PS : 16'bz;  // Controlled_Buffer controlled_buffer_33
  or or_14 (or_14_out, br_abs_flags_d[1], br_abs_flags_d[2]);
  not not_12 (not_12_out, or_14_out);
  Priority_Encoder priority_encoder_3 (
    .in0(_0op), .in1(_1op), .in2(_2op), .in3(mem2), .in4(imm6), .in5(imm9), .in6(mem3),
    .in7(priority_encoder_4_gs), .out(priority_encoder_3_out));  // open: en_in, gs, en_out
  Priority_Encoder priority_encoder_4 (
    .in0(br_abs), .in1(or_12_out), .in2(alu3_ind), .in3(alu3), .in4(br_rel_p), .in5(br_rel_n),
    .in6(or_13_out), .in7(fetch), .out(priority_encoder_4_out), .gs(priority_encoder_4_gs));  // open: en_in, en_out
  or or_15 (or_15_out[0], alu3, alu3_ind);
  Decoder #(.disabled(0)) decoder_6 (.out0(jsr), .out1(rti), .sel(br_abs_flags_d[0]), .en(and_41_out));
  and and_41 (and_41_out, not_12_out, br_abs_flags_d[3], _0op);
  Multiplexer #(.select(3), .width(4), .disabled(0), .enable("false")) multiplexer_10 (
    .in0(br_abs_flags_d), .in1({alu_op_d0[0], imm6_d, br_abs_flags_d[3]}), .in2({alu_op_d1[0], alu_op_d0}),
    .in3({alu_op_d1[0], alu_op_d0}), .in4({br_rel_flags_d[3], alu_op_d1}),
    .in5({br_rel_flags_d[3], alu_op_d1}), .in6({br_rel_flags_d[3], alu_op_d1}), .in7(bit_extender_9_out),
    .out(multiplexer_10_out), .sel(priority_encoder_3_out));
  assign bit_extender_9_out = {{1{1'b0}}, priority_encoder_4_out};  // Bit_Extender bit_extender_9
  or or_16 (or_16_out, shifts, alu2, or_15_out[0]);
  Shifter #(.width(16)) shifter_1 (.in(multiplexer_9_out), .\dist (4'b0001), .out(shifter_1_out));
  Shifter #(.width(16)) shifter_2 (.in(multiplexer_9_out), .\dist (4'b0010), .out(shifter_2_out));
  Multiplexer #(.width(3), .enable("false")) multiplexer_11 (
    .in0(3'b001), .in1({shifts, alu2, or_15_out[0]}), .out(alu_op_type), .sel(or_16_out));
  Multiplexer #(.width(16), .disabled(0), .enable("false")) multiplexer_12 (
    .in0(multiplexer_9_out), .in1(shifter_1_out), .out(multiplexer_12_out), .sel(imm_shift));
  Multiplexer #(.width(16), .disabled(0), .enable("false")) multiplexer_13 (
    .in0(shifter_2_out), .in1(or_17_out), .out(multiplexer_13_out), .sel(phase[0]));
  assign or_17_out = shifter_2_out | 16'h2;  // OR_Gate or_17, 16 bits wide
  not not_13 (not_13_out, or_18_out);
  or or_18 (or_18_out, io_phase, clk_inhibit);
  assign pull_resistor_3_node = rd_wr_prime ? bus_control_1_to_bus : 16'bz;  // Controlled_Buffer controlled_buffer_34
  Multiplexer #(.width(16), .disabled(0), .enable("false")) multiplexer_14 (
    .in0(multiplexer_12_out), .in1(multiplexer_13_out), .out(imm), .sel(\int ));
  and and_42 (word, word_t, not_13_out);
  bus_control bus_control_1 (
    .sign_extend(sign_extend), .odd_address(address[0]), .word(word_t), .clk_no_inhibit(clk_no_inhibit),
    .from_bus(pull_resistor_3_node), .data_in(data_in), .inc_address(inc_address), .clk_inhibit(clk_inhibit),
    .data_out(data_out), .to_bus(bus_control_1_to_bus), .phase(io_phase));
  Comparator #(.width(28)) comparator_3 (.a({28{1'b0}}), .b(rom_1_data), .eq(comparator_3_eq));  // open: gt, lt
  and and_43 (exc_trig_sp, rom_1_data[25], pull_resistor_3_node[0]);
  and and_44 (exc_trig_pc, pull_resistor_3_node[0], rom_1_data[11]);
  ROM #(.addrWidth(10), .dataWidth(28)) rom_1 (
    .addr({phase, priority_encoder_3_out, multiplexer_10_out}), .data(rom_1_data));  // open: sel
  ROM #(.addrWidth(10), .dataWidth(28)) rom_2 (
    .addr({phase, priority_encoder_3_out, multiplexer_10_out}), .data(rom_2_data));  // open: sel
  or or_19 (or_19_out, _1op, alu3_ind);
  Multiplexer #(.width(3), .disabled(0), .enable("false")) multiplexer_15 (
    .in0(alu_op_d0), .in1(br_abs_flags_d[2:0]), .out(rs1), .sel(or_19_out));
  Multiplexer #(.width(3), .disabled(0), .enable("false")) multiplexer_16 (
    .in0({imm6_d, br_abs_flags_d[3]}), .in1(br_abs_flags_d[2:0]), .out(rs0), .sel(imm6));
  and and_45 (exc_trig_invalid_inst, comparator_3_eq, not_14_out);
  not not_14 (not_14_out, exc_latch);
  Multiplexer #(.width(28), .enable("false")) multiplexer_17 (
    .in0(rom_1_data), .in1(rom_2_data), .out(multiplexer_17_out), .sel(exc_triggered));
  and and_46 (and_46_out, alu_op_d1[1], alu_op_d1[2], br_rel_flags_d[3]);
  Multiplexer #(.width(28), .enable("false")) multiplexer_18 (
    .in0(multiplexer_17_out), .in1(28'h8000000),
    .out({CUT, word_t, sp_latch, sp_inc, sp_dec, sp_asrtD, sp_asrt0, sign_extend, rd_wr_prime, r_latch, r_asrtD, r_asrt1, r_asrt0, ps_latch_word, ps_latch_flags, ps_asrtD, pc_latch, pc_inc, pc_asrtD, pc_asrt0, mem, imm_shift, imm_extend_negative, imm_asrtD, imm_asrt1, fp_asrt0, data_ins_prime, alu_asrtD}),
    .sel(or_20_out));
  or or_20 (or_20_out, status[1], startup, and_47_out);
  and and_47 (and_47_out, latch_int, fetch);
  and and_48 (and_48_out, imm6, and_46_out);
  or or_21 (arith_carry, shifts, alu3);
  or or_22 (or_22_out, alu2, alu3_ind);
  Multiplexer #(.width(3), .enable("false")) multiplexer_19 (
    .in0(3'b101), .in1(3'b110), .out(multiplexer_19_out), .sel(and_48_out));
  Multiplexer #(.width(3), .enable("false")) multiplexer_20 (
    .in0(alu_op_d1), .in1(alu_op_d0), .out(multiplexer_20_out), .sel(or_22_out));
  or or_23 (or_23_out, or_22_out, arith_carry);
  Multiplexer #(.width(3), .enable("false")) multiplexer_21 (
    .in0(multiplexer_19_out), .in1(multiplexer_20_out), .out(alu_func), .sel(or_23_out));

  // Other names for the same wires on the sheet: data = data_ins_prime; read = rd_wr_prime;
  //   address_out[15:0] = address; CVZN[3] = cout; direct_exc_vec[5:0] = exc_vec; exc_trig_ext = EXC;
  //   imm9_d[8:0] = {alu_op_d0, imm6_d, br_abs_flags_d}; op_type_d0[3:0] = br_abs_flags_d;
  //   rd[2:0] = br_abs_flags_d[2:0]; rd_d[2:0] = br_abs_flags_d[2:0];
  //   imm6_d (some bits) = {alu_op_d0, br_abs_flags_d[3]};
  //   op_type_d1[3:0] = {alu_op_d0[0], imm6_d, br_abs_flags_d[3]}; rs0_d[2:0] = {imm6_d, br_abs_flags_d[3]};
  //   op_type_d2[3:0] = {alu_op_d1[0], alu_op_d0}; rs1_d[2:0] = alu_op_d0; shift_count_d[2:0] = alu_op_d0;
  //   br_rel_flags_d[2:0] = alu_op_d1; op_type_d3[3:0] = {br_rel_flags_d[3], alu_op_d1};
  //   XY[1:0] = {br_rel_flags_d[3], alu_op_d1[2]}; Y = alu_op_d1[2]; X = br_rel_flags_d[3]; pc_value[15:0] = PC;
  //   ps_value[15:0] = PS; cin = PS[3]; int_en = PS[15]; sp_value[15:0] = SP

  // Notes on the sheet:
  //   data_in: pull=down
  //   clock: pull=down
  //   hold: pull=down
  //   IRQ: pull=down
  //   EXC: pull=down
  //   0 - running
  //   1 - waiting
  //   2 - halted
  //   3 - fault
  //   3
  //   2
  //   1
  //   int, reset, rti
  //   Double fault: 1. Unrecoverable instruction
  //   2. Multiple exceptions on the same phase
  //   3. Mutiple exceptions across several phases
  //   SP
  //   PС
  //   int, reset
  //   CVZN
  //   PS
  //   1, 3, 5, 7
  //   contents of rom_1 (hex, n*v repeats v):
  //   4*0 4*c000000 4a00282 5280882 ca00282 d280882 ce00082 e280082 ca01082 d284082 ca20082 d2c0082
  //   c0c0580 4a00282 8440000 a020000 8041000 8024000 8040200 8020800 a210001 5*0 804a001 15*0 c0c8082
  //   80c8082 81c8082 c0c8080 80c8080 81c8080 c028082 8028082 8*0 c0c00ce c0c00ee 80c008e 80c00ae 81c008e
  //   81c00ae c0200ce c0200ee 802008e 80200ae 8040010 8040030 804a009 804a029 800a008 800a028 4a01082
  //   4080888 ca00092 ca000b2 a200049 a200069 4a00282 4a00282 8*0 c0d8082 80d8082 81d8082 c0d8080 80d8080
  //   81d8080 c038082 8038082 8*0 c080980 804a001 801a000 805a001 8000949 8000969 8000400 c080580 16*0
  //   c080980 d284082 9*0 8020800 60*0 4a00282 c084088 4*0 8000949 8000969 120*0 4080888 127*0 c084088
  //   contents of rom_2 (hex, n*v repeats v):
  //   4*8000000 4*c000000 4a00282 5280082 4a00282 5280082 4e00082 4280082 4a01082 5280082 4a20082 5280082
  //   c080580 4a00282 400000 20000 1000 20000 200 20000 210001 5*8000000 8001 15*8000000 c088482 8088482
  //   8188482 c088480 8088480 8188480 c028482 8028482 8*8000000 c0804ce c0804ee 808048e 80804ae 818048e
  //   81804ae c0204ce c0204ee 802048e 80204ae 8000410 8000430 800a409 800a429 8008408 8008428 4a01082
  //   4080088 4a00092 4a000b2 8200449 8200469 4a00282 4a00282 8*8000000 c098482 8098482 8198482 c098480
  //   8098480 8198480 c038482 8038482 8*8000000 c080580 8008401 8018400 8018401 8000549 8000569 8000400
  //   c080180 8*0 8*8000000 4080180 5280082 9000400 8800400 9000400 8000400 9000400 8800400 9000400
  //   8800400 8000000 20000 7*8000400 5*8000000 8000400 47*8000000 4a00282 4080088 9000400 9000400 8000000
  //   8000000 149 169 32*8000000 8*0 8*8000000 9000400 800000 9*8000000 9000400 60*8000000 4080088 8000400
  //   4*8000000 9000400 9000400 32*8000000 8*0 9*8000000 8800400 70*8000000 4080088 39*8000000 8*0
  //   80*8000000 1000000 39*8000000 8*0 80*8000000 9000400 39*8000000 8*0 120*8000000 8*0 120*8000000
endmodule

module sp_register (
  input  [15:0] In,
  input  clr,
  input  clk,
  input  plus_2,
  input  en,
  input  minus_2,
  output [15:0] Out,
  output [15:0] Mon
);

  wire count, en_t;
  wire [15:0] incdec2_1_out, multiplexer_1_out;

  Multiplexer #(.width(16), .disabled(0), .enable("false")) multiplexer_1 (
    .in0(In), .in1(incdec2_1_out), .out(multiplexer_1_out), .sel(count));
  Register #(.width(16), .trigger("falling")) register_1 (
    .D(multiplexer_1_out), .en(en_t), .Q(Mon), .clk(clk), .clr(clr));
  or or_1 (count, plus_2, minus_2);
  or or_2 (en_t, count, en);
  incdec2 incdec2_1 (.in(Mon), .out(incdec2_1_out), .inc_dec_prime(plus_2));
  Multiplexer #(.width(16), .disabled(0), .enable("false")) multiplexer_2 (
    .in0(Mon), .in1(incdec2_1_out), .out(Out), .sel(minus_2));

  // Notes on the sheet:
  //   plus_2: pull=down
  //   clk: pull=down
  //   minus_2: pull=down
  //   clr: pull=down
  //   en: pull=up
endmodule

module pc_register (
  input  [15:0] In,
  input  clr,
  input  clk,
  input  en,
  input  plus_2,
  input  asrt_inc,
  input  inverse_inc,
  output [15:0] Out,
  output [15:0] Mon
);

  wire en_t, not_1_out;
  wire [15:0] incdec2_1_out, multiplexer_1_out;

  Multiplexer #(.width(16), .disabled(0), .enable("false")) multiplexer_1 (
    .in0(In), .in1(incdec2_1_out), .out(multiplexer_1_out), .sel(plus_2));
  Register #(.width(16), .trigger("falling")) register_1 (
    .D(multiplexer_1_out), .en(en_t), .Q(Mon), .clk(clk), .clr(clr));
  or or_1 (en_t, plus_2, en);
  incdec2 incdec2_1 (.in(Mon), .out(incdec2_1_out), .inc_dec_prime(not_1_out));
  not not_1 (not_1_out, inverse_inc);
  Multiplexer #(.width(16), .disabled(0), .enable("false")) multiplexer_2 (
    .in0(Mon), .in1(incdec2_1_out), .out(Out), .sel(asrt_inc));

  // Other names for the same wires on the sheet: count = plus_2

  // Notes on the sheet:
  //   asrt_inc: pull=down
  //   clr: pull=down
  //   clk: pull=down
  //   inverse_inc: pull=down
  //   en: pull=up
  //   plus_2: pull=down
endmodule

module ps_register (
  input  [3:0] flags,
  input  [15:0] word,
  input  clk,
  input  latch_word,
  input  latch_flags,
  input  ei,
  input  di,
  output [3:0] out_flags,
  output [15:0] out
);

  wire or_1_out, or_3_out, set_int_flag;
  wire [15:0] multiplexer_1_out, multiplexer_2_out;

  Multiplexer #(.width(16), .enable("false")) multiplexer_1 (
    .in0({out[15:4], flags}), .in1({ei, out[14:0]}), .out(multiplexer_1_out), .sel(set_int_flag));
  Multiplexer #(.width(16), .enable("false")) multiplexer_2 (
    .in0(multiplexer_1_out), .in1(word), .out(multiplexer_2_out), .sel(latch_word));
  or or_1 (or_1_out, latch_word, latch_flags);
  or or_2 (set_int_flag, ei, di);
  Register #(.width(16), .trigger("falling")) register_1 (
    .D(multiplexer_2_out), .en(or_3_out), .Q(out), .clk(clk));  // open: clr
  or or_3 (or_3_out, or_1_out, set_int_flag);
  Bit_Extender #(.in_width(16), .out_width(4)) bit_extender_1 (.in(out), .out(out_flags));

  // Notes on the sheet:
  //   latch_word: pull=down
  //   flags: pull=down
  //   latch_flags: pull=down
  //   clk: pull=down
  //   word: pull=down
  //   ei: pull=down
  //   di: pull=down
endmodule

module address_adder (
  input  [15:0] A,
  input  [15:0] B,
  output [16:0] Out
);

  Adder #(.width(16)) adder_1 (.a(A), .b(B), .out(Out[15:0]), .cout(Out[16]));  // open: cin

  // Notes on the sheet:
  //   B: pull=down
  //   A: pull=down
endmodule

module address_expander (
  input  [15:0] A,
  input  B,
  output [16:0] Out
);


  assign Out = {B, A};

  // Notes on the sheet:
  //   B: pull=down
  //   A: pull=down
endmodule

module incdec16 (
  input  [15:0] in,
  input  inc_dec_prime,
  output [15:0] out
);

  wire [15:0] multiplexer_1_out;

  Multiplexer #(.width(16), .enable("false")) multiplexer_1 (
    .in0({16{1'b1}}), .in1(16'h1), .out(multiplexer_1_out), .sel(inc_dec_prime));
  Adder #(.width(16)) adder_1 (.a(in), .b(multiplexer_1_out), .out(out));  // open: cin, cout

  // Notes on the sheet:
  //   inc_dec_prime: pull=up
endmodule

module incdec2 (
  input  [15:0] in,
  input  inc_dec_prime,
  output [15:0] out
);

  wire [15:0] multiplexer_1_out;

  Multiplexer #(.width(16), .enable("false")) multiplexer_1 (
    .in0(16'hfffe), .in1(16'h2), .out(multiplexer_1_out), .sel(inc_dec_prime));
  Adder #(.width(16)) adder_1 (.a(in), .b(multiplexer_1_out), .out(out));  // open: cin, cout

  // Notes on the sheet:
  //   inc_dec_prime: pull=up
endmodule

module bus_control (
  input  sign_extend,
  input  odd_address,
  input  word,
  input  clk_no_inhibit,
  input  [15:0] from_bus,
  input  [15:0] data_in,
  output inc_address,
  output clk_inhibit,
  output phase,
  output [15:0] data_out,
  output [15:0] to_bus
);

  wire and_1_out;
  wire [7:0] bit_extender_1_out, register_1_q;
  wire [15:0] bytes_swap_1_out, make_byte_2_out, multiplexer_1_out, multiplexer_3_out, multiplexer_5_out,
       n2s_compliment_1_out;

  Bit_Extender #(.in_width(16), .out_width(8)) bit_extender_1 (.in(data_in), .out(bit_extender_1_out));
  and and_1 (and_1_out, clk_inhibit, clk_no_inhibit);
  Register #(.trigger("falling")) register_1 (
    .D(bit_extender_1_out), .Q(register_1_q), .clk(and_1_out));  // open: en, clr
  and and_2 (clk_inhibit, odd_address, word);
  make_byte make_byte_1 ();  // open: In, Out
  Multiplexer #(.width(16), .disabled(0), .enable("false")) multiplexer_1 (
    .in0(from_bus), .in1(bytes_swap_1_out), .out(multiplexer_1_out), .sel(inc_address));
  bytes_swap bytes_swap_1 (.In(from_bus), .Out(bytes_swap_1_out));
  make_byte make_byte_2 (.In(data_in), .Out(make_byte_2_out));
  _2s_compliment u_2s_compliment_1 (.In(data_in), .Out(n2s_compliment_1_out));
  D_Flip_Flop #(.trigger("falling")) d_ff_1 (
    .clk(clk_no_inhibit), .D(clk_inhibit), .Q(inc_address));  // open: Qn, preset, en, reset
  Multiplexer #(.width(16), .disabled(0), .enable("false")) multiplexer_2 (
    .in0(from_bus), .in1(multiplexer_1_out), .out(data_out), .sel(word));
  Multiplexer #(.width(16), .disabled(0), .enable("false")) multiplexer_3 (
    .in0(make_byte_2_out), .in1(n2s_compliment_1_out), .out(multiplexer_3_out), .sel(sign_extend));
  Multiplexer #(.width(16), .disabled(0), .enable("false")) multiplexer_4 (
    .in0(multiplexer_3_out), .in1(multiplexer_5_out), .out(to_bus), .sel(word));
  Multiplexer #(.width(16), .disabled(0), .enable("false")) multiplexer_5 (
    .in0(data_in), .in1({bit_extender_1_out, register_1_q}), .out(multiplexer_5_out), .sel(inc_address));

  assign phase = inc_address;

  // Other names for the same wires on the sheet: odd = odd_address

  // Notes on the sheet:
  //   data_in: pull=down
endmodule

module alu (
  input  [15:0] A,
  input  [15:0] B,
  input  Cin,
  input  [2:0] func,
  input  [2:0] op_type,
  input  [2:0] shift_count,
  output C,
  output V,
  output Z,
  output N,
  output [15:0] S
);

  wire adc, add, adder16_1_cout, adder16_1_v, adder_carry, \and , and_3_out, and_4_out,
       barrel_shifter_1_cout, bic, multiplexer_7_out, multiplexer_8_out, neg, \not , \or , or_2_out,
       or_3_out, rcl, rcr, rol, ror, sbc, scl, shl, shr, shra, sub, sxt, \xor ;
  wire [15:0] adder16_1_s, and_1_out, and_2_out, barrel_shifter_1_out, make_byte_1_out, multiplexer_1_out,
       multiplexer_2_out, multiplexer_3_out, multiplexer_4_out, multiplexer_5_out, multiplexer_6_out,
       n2s_compliment_1_out, not_1_out, not_2_out, not_3_out, not_4_out, or_1_out, xor_1_out;

  Decoder #(.select(3), .disabled(0)) decoder_1 (
    .out0(\and ), .out1(\or ), .out2(\xor ), .out3(bic), .out4(add), .out5(adc), .out6(sub), .out7(sbc),
    .sel(func), .en(op_type[0]));
  Decoder #(.select(3), .disabled(0)) decoder_2 (
    .out0(neg), .out1(\not ), .out2(sxt), .out3(scl), .sel(func), .en(op_type[1]));  // open: out4, out5, out6, out7
  Decoder #(.select(3), .disabled(0)) decoder_3 (
    .out0(shl), .out1(shr), .out2(shra), .out3(rol), .out4(ror), .out5(rcl), .out6(rcr), .sel(func),
    .en(op_type[2]));  // open: out7
  assign and_1_out = A & B;  // AND_Gate and_1, 16 bits wide
  assign or_1_out = A | B;  // OR_Gate or_1, 16 bits wide
  assign xor_1_out = A ^ B;  // XOR_Gate xor_1, 16 bits wide
  assign and_2_out = A & not_1_out;  // AND_Gate and_2, 16 bits wide
  assign not_1_out = ~B;  // NOT_Gate not_1, 16 bits wide
  Multiplexer #(.width(16), .enable("false")) multiplexer_1 (
    .in0(A), .in1(not_2_out), .out(multiplexer_1_out), .sel(neg));
  assign not_2_out = ~A;  // NOT_Gate not_2, 16 bits wide
  Multiplexer #(.width(16), .enable("false")) multiplexer_2 (
    .in0(B), .in1(not_3_out), .out(multiplexer_2_out), .sel(or_2_out));
  assign not_3_out = ~B;  // NOT_Gate not_3, 16 bits wide
  or or_2 (or_2_out, sub, sbc);
  assign not_4_out = ~A;  // NOT_Gate not_4, 16 bits wide
  _2s_compliment u_2s_compliment_1 (.In(A), .Out(n2s_compliment_1_out));
  make_byte make_byte_1 (.In(A), .Out(make_byte_1_out));
  barrel_shifter barrel_shifter_1 (
    .In(A), .cin(Cin), .shift_type(func), .distance(shift_count), .Out(barrel_shifter_1_out),
    .cout(barrel_shifter_1_cout));
  adder16 adder16_1 (
    .A(multiplexer_1_out), .B(multiplexer_2_out), .S(adder16_1_s), .Cin(adder_carry), .Cout(adder16_1_cout),
    .V(adder16_1_v));
  Multiplexer #(.select(2), .width(16), .enable("false")) multiplexer_3 (
    .in0(adder16_1_s), .in1(not_4_out), .in2(n2s_compliment_1_out), .in3(make_byte_1_out),
    .out(multiplexer_3_out), .sel(func[1:0]));
  // NOT_Gate not_5 is placed but not wired
  Multiplexer #(.select(2), .width(16), .enable("false")) multiplexer_4 (
    .in0(and_1_out), .in1(or_1_out), .in2(xor_1_out), .in3(and_2_out), .out(multiplexer_4_out),
    .sel(func[1:0]));
  Multiplexer #(.width(16), .enable("false")) multiplexer_5 (
    .in0(multiplexer_4_out), .in1(adder16_1_s), .out(multiplexer_5_out), .sel(func[2]));
  and and_3 (and_3_out, sbc, Cin);
  or or_3 (or_3_out, and_3_out, and_4_out);
  and and_4 (and_4_out, Cin, adc);
  or or_4 (adder_carry, or_3_out, neg, sub);
  Multiplexer #(.width(16), .enable("false")) multiplexer_6 (
    .in0(multiplexer_5_out), .in1(multiplexer_3_out), .out(multiplexer_6_out), .sel(op_type[1]));
  Multiplexer #(.enable("false")) multiplexer_7 (
    .in0(adder16_1_cout), .in1(1'b0), .out(multiplexer_7_out), .sel(op_type[1]));
  Multiplexer #(.enable("false")) multiplexer_8 (
    .in0(adder16_1_v), .in1(1'b0), .out(multiplexer_8_out), .sel(op_type[1]));
  Multiplexer #(.width(16), .enable("false")) multiplexer_9 (
    .in0(multiplexer_6_out), .in1(barrel_shifter_1_out), .out({N, S[14:0]}), .sel(op_type[2]));
  Multiplexer #(.enable("false")) multiplexer_10 (
    .in0(multiplexer_7_out), .in1(barrel_shifter_1_cout), .out(C), .sel(op_type[2]));
  Multiplexer #(.enable("false")) multiplexer_11 (.in0(multiplexer_8_out), .in1(1'b0), .out(V), .sel(op_type[2]));
  // Probe on {N, S[14:0]}
  // NOT_Gate not_6 is placed but not wired
  zero16 zero16_1 (.in({N, S[14:0]}), .zero(Z));
  // NOT_Gate not_7 is placed but not wired

  assign S[15] = N;

  // Other names for the same wires on the sheet: _3op = op_type[0]; _2op = op_type[1]; shifts = op_type[2]

  // Notes on the sheet:
  //   B: pull=down
  //   op_type: pull=down
  //   A: pull=down
  //   func: pull=down
  //   Cin: pull=down
  //   shift_count: pull=down
endmodule

module multiplier (
  input  [15:0] A,
  input  [15:0] B,
  input  clk,
  input  reset,
  input  count,
  output [15:0] SLow,
  output [15:0] SHigh
);

  wire adder_1_cout, d_ff_1_q;
  wire [1:0] counter_1_q;
  wire [7:0] bit_extender_1_out, demultiplexer_1_out0, demultiplexer_1_out1, demultiplexer_1_out3,
       demultiplexer_2_out3, multiplexer_1_out, multiplexer_2_out, multiplexer_3_out, multiplexer_4_out;
  wire [15:0] adder_1_out, multiplier_1_out;

  assign bit_extender_1_out = {{7{1'b0}}, d_ff_1_q};  // Bit_Extender bit_extender_1
  Counter #(.width(2), .max('h3), .trigger("falling")) counter_1 (
    .count(count), .Q(counter_1_q), .clk(clk), .clr(reset));  // open: load, D, carry
  Multiplexer #(.select(2), .width(8), .enable("false")) multiplexer_1 (
    .in0(SLow[7:0]), .in1(SLow[15:8]), .in2(SLow[15:8]), .in3(SHigh[7:0]), .out(multiplexer_1_out),
    .sel(counter_1_q));
  Multiplexer #(.select(2), .width(8), .enable("false")) multiplexer_2 (
    .in0(SLow[15:8]), .in1(bit_extender_1_out), .in2(SHigh[7:0]), .in3(bit_extender_1_out),
    .out(multiplexer_2_out), .sel(counter_1_q));
  Adder #(.width(16)) adder_1 (
    .a(multiplier_1_out), .b({multiplexer_2_out, multiplexer_1_out}), .out(adder_1_out), .cout(adder_1_cout));  // open: cin
  D_Flip_Flop d_ff_1 (.clk(clk), .D(adder_1_cout), .Q(d_ff_1_q), .reset(reset));  // open: Qn, preset, en
  Multiplexer #(.width(8), .enable("false")) multiplexer_3 (
    .in0(A[7:0]), .in1(A[15:8]), .out(multiplexer_3_out), .sel(counter_1_q[0]));
  Register register_1 (.D(demultiplexer_1_out3), .en(count), .Q(SHigh[7:0]), .clk(clk), .clr(reset));
  Register register_2 (.D(demultiplexer_2_out3), .en(count), .Q(SHigh[15:8]), .clk(clk), .clr(reset));
  Multiplexer #(.width(8), .enable("false")) multiplexer_4 (
    .in0(B[7:0]), .in1(B[15:8]), .out(multiplexer_4_out), .sel(counter_1_q[1]));
  Multiplier multiplier_1 (
    .a(multiplexer_4_out), .b(multiplexer_3_out), .out(multiplier_1_out[7:0]), .cout(multiplier_1_out[15:8]));  // open: cin
  Register register_3 (.D(demultiplexer_1_out1), .en(count), .Q(SLow[15:8]), .clk(clk), .clr(reset));
  Demultiplexer #(.select(2), .width(8), .tristate("true"), .enable("false")) demultiplexer_1 (
    .out0(demultiplexer_1_out0), .out1(demultiplexer_1_out1), .out2(demultiplexer_1_out1),
    .out3(demultiplexer_1_out3), .in(adder_1_out[7:0]), .sel(counter_1_q));
  Demultiplexer #(.select(2), .width(8), .tristate("true"), .enable("false")) demultiplexer_2 (
    .out0(demultiplexer_1_out1), .out1(demultiplexer_1_out3), .out2(demultiplexer_1_out3),
    .out3(demultiplexer_2_out3), .in(adder_1_out[15:8]), .sel(counter_1_q));
  Register register_4 (.D(demultiplexer_1_out0), .en(count), .Q(SLow[7:0]), .clk(clk), .clr(reset));
endmodule

module barrel_shifter (
  input  [15:0] In,
  input  cin,
  input  [2:0] shift_type,
  input  [2:0] distance,
  output [15:0] Out,
  output cout
);

  wire [4:0] adder_1_out, bit_extender_1_out;
  wire [15:0] shifter_4_out, shifter_5_out;
  wire [16:0] shifter_1_out, shifter_2_out, shifter_3_out, shifter_6_out, shifter_7_out;

  assign bit_extender_1_out = {{2{1'b0}}, distance};  // Bit_Extender bit_extender_1
  Adder #(.width(5)) adder_1 (.a(bit_extender_1_out), .b(5'b00001), .out(adder_1_out));  // open: cin, cout
  Shifter #(.width(17)) shifter_1 (.in({{2{In[15]}}, In[14:0]}), .\dist (adder_1_out), .out(shifter_1_out));
  Shifter #(.width(17), .shift("lr")) shifter_2 (.in({In, In[0]}), .\dist (adder_1_out), .out(shifter_2_out));
  Shifter #(.width(17), .shift("ar")) shifter_3 (.in({In, In[0]}), .\dist (adder_1_out), .out(shifter_3_out));
  Shifter #(.width(16), .shift("rl")) shifter_4 (.in(In), .\dist (adder_1_out[3:0]), .out(shifter_4_out));
  Shifter #(.width(16), .shift("rr")) shifter_5 (.in(In), .\dist (adder_1_out[3:0]), .out(shifter_5_out));
  Shifter #(.width(17), .shift("rl")) shifter_6 (.in({cin, In}), .\dist (adder_1_out), .out(shifter_6_out));
  Shifter #(.width(17), .shift("rr")) shifter_7 (.in({In, cin}), .\dist (adder_1_out), .out(shifter_7_out));
  Multiplexer #(.select(3), .width(16), .enable("false")) multiplexer_1 (
    .in0(shifter_1_out[15:0]), .in1(shifter_2_out[16:1]), .in2(shifter_3_out[16:1]), .in3(shifter_4_out),
    .in4(shifter_5_out), .in5(shifter_6_out[15:0]), .in6(shifter_7_out[16:1]), .out(Out), .sel(shift_type));  // open: in7
  Multiplexer #(.select(3), .enable("false")) multiplexer_2 (
    .in0(shifter_1_out[16]), .in1(shifter_2_out[0]), .in2(shifter_3_out[0]), .in3(shifter_4_out[0]),
    .in4(shifter_5_out[15]), .in5(shifter_6_out[16]), .in6(shifter_7_out[0]), .out(cout), .sel(shift_type));  // open: in7

  // Other names for the same wires on the sheet: value[15:0] = In; type[2:0] = shift_type

  // Notes on the sheet:
  //   shift_type: pull=down
  //   cin: pull=down
  //   In: pull=down
  //   distance: pull=down
  //   shl
  //   shr
  //   shra
  //   rol
  //   ror
  //   rcl
  //   rcr
endmodule

module adder16 (
  input  Cin,
  input  [15:0] A,
  input  [15:0] B,
  output [15:0] S,
  output Cout,
  output V
);

  wire [15:0] and_1_out, and_2_out, and_3_out;
  wire [15:1] or_1_out;

  // Probe on A
  // Probe on B
  assign S = A ^ {or_1_out, Cin} ^ B;  // XOR_Gate xor_1, 16 bits wide
  assign and_1_out = B & A;  // AND_Gate and_1, 16 bits wide
  assign and_2_out = B & {or_1_out, Cin};  // AND_Gate and_2, 16 bits wide
  assign and_3_out = A & {or_1_out, Cin};  // AND_Gate and_3, 16 bits wide
  assign {Cout, or_1_out} = and_1_out | and_2_out | and_3_out;  // OR_Gate or_1, 16 bits wide
  // Probe on S
  xor xor_2 (V, or_1_out[15], Cout);

  // Notes on the sheet:
  //   Cin: pull=down
  //   A: pull=down
  //   B: pull=down
endmodule

module adder8 (
  input  Cin,
  input  [7:0] A,
  input  [7:0] B,
  output [7:0] S,
  output Cout,
  output V
);

  wire [7:0] and_1_out, and_2_out, and_3_out;
  wire [7:1] or_1_out;

  // Probe on A
  // Probe on B
  assign S = A ^ {or_1_out, Cin} ^ B;  // XOR_Gate xor_1, 8 bits wide
  assign and_1_out = B & A;  // AND_Gate and_1, 8 bits wide
  assign and_2_out = B & {or_1_out, Cin};  // AND_Gate and_2, 8 bits wide
  assign and_3_out = A & {or_1_out, Cin};  // AND_Gate and_3, 8 bits wide
  assign {Cout, or_1_out} = and_1_out | and_2_out | and_3_out;  // OR_Gate or_1, 8 bits wide
  // Probe on S
  xor xor_2 (V, or_1_out[7], Cout);

  // Notes on the sheet:
  //   B: pull=down
  //   Cin: pull=down
  //   A: pull=down
endmodule

module branch_logic (
  input  [3:0] cccc,
  input  [3:0] CVZN,
  output go
);

  wire and_1_out, and_2_out, and_3_out, and_4_out, and_5_out, and_6_out, and_7_out, decoder_1_out0,
       decoder_1_out1, decoder_1_out2, decoder_1_out3, decoder_2_out0, decoder_2_out1, decoder_2_out2,
       decoder_2_out3, not_1_out, not_2_out, or_1_out, xnor_1_out;

  not not_1 (not_1_out, cccc[3]);
  Decoder #(.select(2), .disabled(0)) decoder_1 (
    .out0(decoder_1_out0), .out1(decoder_1_out1), .out2(decoder_1_out2), .out3(decoder_1_out3),
    .sel(cccc[2:1]), .en(not_1_out));
  and and_1 (and_1_out, decoder_1_out0, CVZN[1]);
  and and_2 (and_2_out, decoder_1_out1, CVZN[3]);
  and and_3 (and_3_out, decoder_1_out2, CVZN[0]);
  and and_4 (and_4_out, decoder_1_out3, CVZN[2]);
  not not_2 (not_2_out, CVZN[1]);
  xnor xnor_1 (xnor_1_out, CVZN[0], CVZN[2]);
  Decoder #(.select(2), .disabled(0)) decoder_2 (
    .out0(decoder_2_out0), .out1(decoder_2_out1), .out2(decoder_2_out2), .out3(decoder_2_out3),
    .sel(cccc[2:1]), .en(cccc[3]));
  and and_5 (and_5_out, decoder_2_out0, not_2_out, CVZN[3]);
  and and_6 (and_6_out, xnor_1_out, decoder_2_out1);
  and and_7 (and_7_out, not_2_out, xnor_1_out, decoder_2_out2);
  or or_1 (or_1_out, and_1_out, and_2_out, and_3_out, and_4_out, and_5_out, and_6_out, and_7_out, decoder_2_out3);
  xor xor_1 (go, cccc[0], or_1_out);

  // Notes on the sheet:
  //   N
  //   Z
  //   V
  //   C
  //   EQ
  //   HS/CS
  //   MI
  //   VS
  //   N=V
  //   Z'
  //   HI
  //   GE
  //   GT
  //   <always>
endmodule

module zero8 (
  input  [7:0] in,
  output zero
);

  nor nor_1 (zero, in[0], in[1], in[2], in[3], in[4], in[5], in[6], in[7]);
endmodule

module zero16 (
  input  [15:0] in,
  output zero
);

  wire nor_1_out, nor_2_out;

  nor nor_1 (nor_1_out, in[0], in[1], in[2], in[3], in[4], in[5], in[6], in[7]);
  nor nor_2 (nor_2_out, in[8], in[9], in[10], in[11], in[12], in[13], in[14], in[15]);
  and and_1 (zero, nor_1_out, nor_2_out);
endmodule

module _2s_compliment (
  input  [15:0] In,
  output [15:0] Out
);

  wire [7:0] bit_extender_1_out;

  Bit_Extender #(.in_width(16), .out_width(8)) bit_extender_1 (.in(In), .out(bit_extender_1_out));
  assign Out = {{8{bit_extender_1_out[7]}}, bit_extender_1_out};  // Bit_Extender bit_extender_2
endmodule

module make_byte (
  input  [15:0] In,
  output [15:0] Out
);

  wire [7:0] bit_extender_1_out;

  Bit_Extender #(.in_width(16), .out_width(8)) bit_extender_1 (.in(In), .out(bit_extender_1_out));
  assign Out = {{8{1'b0}}, bit_extender_1_out};  // Bit_Extender bit_extender_2
endmodule

module bytes_swap (
  input  [15:0] In,
  output [15:0] Out
);


  assign Out = {In[7:0], In[15:8]};
endmodule
